# Fritzing sketch DiagramaBancada (saved by Fritzing 1.0.6)

parts:
  A3 = MH-ET Live Minikit for ESP32
  HLK-PM3 = HLK-PM01
  RY2 = srd-05vdc-sl-c
  R5 = Resistor [tolerance=±5% resistance=510 package="0402 [SMD]"]
  R6 = Resistor [tolerance=±5% resistance=1k package="0402 [SMD]"]
  Q2 = NPN-Transistor [package="TO92 [THT]"]
  U2 = Sharp PC817 [part_number=PC817XI package=SMT]
  D2 = Diode [package=diode-1n4001]
  A4 = yf-s401 flow sensor [package=THT]
  A5 = DHT22 module

nets:
  N1: A3.GND, HLK-PM3.-Vo, Q2.C, A4.pin2, A5.-
  N2: A3.IO23, U2.Pin_2
  N3: A3.3.3V, R6.Pin_1, A4.pin1, A5.+
  N4: A3.IO22, A4.pin3
  N5: A3.IO21, A5.Out
  N6: A3.VCC, HLK-PM3.+Vo, RY2.pin_4, U2.Pin_4, D2.C
  N7: HLK-PM3.AC#0, RY2.pin_5
  N8: RY2.pin_1, Q2.E, D2.A
  N9: R5.Pin_0, U2.Pin_3
  N10: R5.Pin_1, Q2.B
  N11: R6.Pin_0, U2.Pin_1

custom parts:
  MH-ET Live Minikit for ESP32: MH-ET Live Minikit for ESP32 ( http://mh.nodebb.com/topic/8/mh-et-live-minikit-for-esp32/2/) PCB footprint is invalid.
  yf-s401 flow sensor: Flow sensors sit in line with your water line, and uses a pinwheel sensor to measure how much liquid has moved through it.
  DHT22 module: DHT22 module. Pins VCC Data GND.
