# Fritzing sketch DiagramaReservatorio (saved by Fritzing 1.0.6)

parts:
  M1 = ph-4502c [package=THT]
  A1 = MH-ET Live Minikit for ESP32
  A2 = tds-sensor-meter-v1.0_1
  M4 = fc-51 [package=THT]
  M5 = fc-51 [package=THT]
  M6 = fc-51 [package=THT]
  DS1 = DS18B20 1-Wire Temperature Sensor Probe
  R1 = Resistor [tolerance=±5% resistance=4.7k package="0402 [SMD]"]  # not connected
  HLK-PM2 = HLK-PM01
  RY1 = srd-05vdc-sl-c
  R2 = Resistor [tolerance=±5% resistance=1k package="0402 [SMD]"]
  U1 = Sharp PC817 [part_number=PC817XI package=SMT]
  Q1 = NPN-Transistor [package="TO92 [THT]"]
  R3 = Resistor [tolerance=±5% resistance=510 package="0402 [SMD]"]
  D1 = Diode [package=diode-1n4001]

nets:
  N1: M1.pin3, A1.IO32
  GND: M1.pin4, M1.pin5, A1.GND, A2.pin3, M4.pin3, M5.pin3, M6.pin3, DS1.GND, HLK-PM2.-Vo, Q1.C
  N2: M1.pin6, A1.VCC, HLK-PM2.+Vo, RY1.pin_4, U1.Pin_4, D1.C
  N3: A1.IO35, M6.pin2
  N4: A1.IO33, A2.pin1
  N5: A1.IO23, U1.Pin_2
  3.3V: A1.3.3V, A2.pin2, M4.pin1, M5.pin1, M6.pin1, DS1.VDD, R2.Pin_1
  N6: A1.IO21, M5.pin2
  N7: A1.IO27, DS1.DQ
  N8: A1.IO25, M4.pin2
  N9: HLK-PM2.AC#0, RY1.pin_5
  N10: RY1.pin_1, Q1.E, D1.A
  N11: R2.Pin_0, U1.Pin_1
  N12: U1.Pin_3, R3.Pin_0
  N13: Q1.B, R3.Pin_1

custom parts:
  ph-4502c: ph-4502c PH Meter.
  MH-ET Live Minikit for ESP32: MH-ET Live Minikit for ESP32 ( http://mh.nodebb.com/topic/8/mh-et-live-minikit-for-esp32/2/) PCB footprint is invalid.
  : TDS Meter V1.0 Development Board Water Meter Filter Measuring Water Sensor Module.
  fc-51: XKC-Y25-NPN Non-Contact Liquid Level Sensor IP67 Waterproof NPN Output Water Level Detector DC 5-12V.
